// Logisim project PC.circ as structural Verilog: 1 circuit, main circuit main
module main (
  input  [31:0] in_1,
  input  [10:0] in_2,
  input  [15:0] in_3,
  input  in_4,
  input  [4:0] in_5,
  input  [1:0] in_6,
  output [19:0] out_7,
  output [19:0] out_8
);

  wire adder_2_cout;
  wire [19:0] adder_2_out, adder_4_out, bit_extender_1_out, bit_extender_2_out, multiplexer_1_out;

  Register #(.width(20)) PC_Register (.D(multiplexer_1_out), .en(1'b1), .clk(in_4), .Q(out_8));  // open: clr
  assign bit_extender_1_out = {{4{in_2[10]}}, {in_2, in_5}};  // Bit_Extender bit_extender_1
  Adder #(.width(20)) adder_1 (.a(out_8), .b(20'h1), .out(out_7), .cin(1'b0));  // open: cout
  Adder #(.width(20)) adder_2 (.a(out_8), .b(bit_extender_1_out), .out(adder_2_out), .cin(1'b0), .cout(adder_2_cout));
  Adder #(.width(20)) adder_3 (.a(out_8), .b(bit_extender_1_out), .out(adder_2_out), .cin(1'b0), .cout(adder_2_cout));
  assign bit_extender_2_out = {{4{in_3[15]}}, in_3};  // Bit_Extender bit_extender_2
  Adder #(.width(20)) adder_4 (.a(bit_extender_2_out), .b(in_1[19:0]), .out(adder_4_out), .cin(1'b0));  // open: cout
  Multiplexer #(.select(2), .width(20), .enable("false")) multiplexer_1 (
    .in0(out_7), .in1(adder_2_out), .in2(adder_4_out), .out(multiplexer_1_out), .sel(in_6));  // open: in3

  // Other names for the same wires on the sheet: ImmL[4:0] = in_5; ImmU[10:0] = in_2; Address[19:0] = out_8;
  //   clock = in_4; Imm16[15:0] = in_3; PC_1[19:0] = out_7; RS1[31:0] = in_1
endmodule
